# Fritzing sketch Sketch (saved by Fritzing 0.9.3b)
breadboards: 1

parts:
  Часть1 = Arduino Uno (Rev3)
  S1 = SWITCH-MOMENTARY-2 [package=tactile-pth]
  S2 = SWITCH-MOMENTARY-2 [package=tactile-pth]
  S3 = SWITCH-MOMENTARY-2 [package=tactile-pth]
  S4 = SWITCH-MOMENTARY-2 [package=tactile-pth]
  Часть2 = BME280
  M1 = ph-4502c [package=THT]
  Capacitive_Soil_Moisture_Sensor1 = Capacitive Soil Moisture Sensor V2.0
  IC1 = ADS1115 16-bit ADC Breakout
  Espessif_Serial_Wifi_Modul_1 = ESP8266 ESP01 [part_number=ESP8266 package=THT]
  S5 = LDR light sensor [package=THT]
  GLCD_128x1 = 128 x 64 Graphic LCD  # not connected
  R1 = Rotary Potentiometer (Small) [maximum_resistance=100kΩ package=THT]
  R2 = Resistor [tolerance=±5% resistance=220 package=THT]

nets:
  N1: Часть1.A4/SDA, Часть2.SDA, IC1.SDA
  N2: Часть1.A5/SCL, Часть2.SCL, IC1.SCL
  N3: Часть1.D2, S2.2
  N4: Часть1.D3_PWM, S3.2
  N5: Часть1.D4, S4.2
  N6: Часть1.D5_PWM, S1.2
  3V3: Часть1.3V3, Часть2.VIN
  5V: Часть1.5V, S1.1, S2.1, S3.1, S4.1, M1.pin6, Capacitive_Soil_Moisture_Sensor1.VCC, IC1.VDD, S5.pin3, R1.leg2, R2.Pin_1
  GND: Часть1.GND, Часть2.GND, M1.pin4, M1.pin5, Capacitive_Soil_Moisture_Sensor1.GND, IC1.GND, Espessif_Serial_Wifi_Modul_1.GND, S5.pin2, R1.leg1
  N7: M1.pin1, IC1.A3
  N8: M1.pin3, IC1.A2
  N9: Capacitive_Soil_Moisture_Sensor1.AOUT, IC1.A1
  N10: IC1.A0, S5.pin1

notes:
  Parts List
  - Arduino Uno
  - 4 Buttons
  - LCD 128x64 (WM-G1206A)
  - BME280
  - pH Sensor
  - Capacitive Soil Moisure Sensor
  - ADS1115
  - ESP-01
  - Light Sensor
  Buttons Order
  From left to right:
  Back, Down, Up, OK
  Ignore the marks here. Wires connected by pins order as they go on WM-G1206A

custom parts:
  ph-4502c: ph-4502c PH Meter.
  ADS1115 16-bit ADC Breakout: ADS1015 12-bit I2C ADC+PGA Breakout
  ESP8266 ESP01: Generic WiFi Module based on the ESP8266 with onboard PCB antenna and UART communications
  LDR light sensor: Light sensor module. 3.3 V to 5V power.
